# Fritzing sketch CameraDemoForAndroidThings (saved by Fritzing 0.9.3b)
breadboards: 1

parts:
  Raspberry_Pi_1 = Raspberry Pi 3 [part_number=RPI-3-V1.2]
  R1 = Resistor [tolerance=±5% resistance=220 package=THT]
  S1 = Pushbutton [package="[THT]"]
  S2 = Pushbutton [package="[THT]"]
  R2 = Resistor [tolerance=±5% resistance=220 package=THT]
  U1 = TCM8240MD [package=tcm8240md]

nets:
  N1: Raspberry_Pi_1.GPIO6, S2.Pin_3, S2.Pin_4, R2.Pin_1
  N2: Raspberry_Pi_1.GPIO21, R1.Pin_1, S1.Pin_3, S1.Pin_4
  N3: Raspberry_Pi_1.5V, R1.Pin_0, S1.Pin_1, S1.Pin_2, S2.Pin_1, S2.Pin_2, R2.Pin_0
  N4: U1.GND, U1.PVDD(2.8V), U1.RESET, U1.SCL, U1.SDA

notes:
  Button A
  Button B
